# Fritzing sketch io_list (saved by Fritzing 0.9.3b)
breadboards: 1

parts:
  Mod1 = Raspberry Pi Pico W
  LED1 = RGB LED (com. cathode, rgb) [package="5 mm [THT]"]
  LED2 = RGB LED (com. cathode, rgb) [package="5 mm [THT]"]
  LED3 = RGB LED (com. cathode, rgb) [package="5 mm [THT]"]
  LED4 = RGB LED (com. cathode, rgb) [package="5 mm [THT]"]
  LED5 = RGB LED (com. cathode, rgb) [package="5 mm [THT]"]
  LED6 = RGB LED (com. cathode, rgb) [package="5 mm [THT]"]
  LED7 = RGB LED (com. cathode, rgb) [package="5 mm [THT]"]
  LED8 = RGB LED (com. cathode, rgb) [package="5 mm [THT]"]  # not connected
  LED9 = RGB LED (com. cathode, rgb) [package="5 mm [THT]"]
  Part1 = DeuLigne 1.1 - The Snootlab's LCD shield for Arduino

nets:
  N1: Mod1.pin_3, Mod1.pin_8, Mod1.pin_13, Mod1.pin_18, Mod1.pin_23, Mod1.pin_28, Mod1.pin_33, Mod1.pin_38
  N2: Mod1.pin_4, LED1.blue_anode
  N3: Mod1.pin_5, LED1.common_cathode
  N4: Mod1.pin_6, LED1.red_anode
  N5: Mod1.pin_7, LED2.blue_anode
  N6: Mod1.pin_9, LED2.common_cathode
  N7: Mod1.pin_10, LED2.red_anode
  N8: Mod1.pin_11, LED4.blue_anode
  N9: Mod1.pin_12, LED4.common_cathode
  N10: Mod1.pin_14, LED4.red_anode
  N11: Mod1.pin_15, LED3.blue_anode
  N12: Mod1.pin_16, LED3.common_cathode
  N13: Mod1.pin_17, LED3.red_anode
  N14: Mod1.pin_19, LED9.blue_anode
  N15: Mod1.pin_20, LED9.common_cathode
  N16: Mod1.pin_21, LED9.red_anode
  N17: Mod1.pin_22, LED7.blue_anode
  N18: Mod1.pin_24, LED7.common_cathode
  N19: Mod1.pin_25, LED7.red_anode
  N20: Mod1.pin_26, LED6.blue_anode
  N21: Mod1.pin_27, LED6.green_anode
  N22: Mod1.pin_29, LED6.red_anode
  N23: Mod1.pin_31, LED5.blue_anode
  N24: Mod1.pin_32, LED5.green_anode
  N25: Mod1.pin_34, LED5.red_anode
  N26: Mod1.pin_37, Part1.GND
  N27: Mod1.pin_39, LED1.green_anode, LED2.green_anode, LED3.green_anode, LED4.green_anode, LED5.common_cathode, LED6.common_cathode, LED7.green_anode, LED9.green_anode, Part1.+5V

custom parts:
  Raspberry Pi Pico W: Raspberry Pi Pico W. Based around the RP2040 microcontroller the Pico W is a low cost microcontroller device bringing Raspberry Pi quality, cost, and easy of use to the microcontroller space. The areas marked KEEPOUT in pcb silkscreen should not have traces running through them to avoid shorts on a soldered in module!
